# Fritzing sketch hassbeam (saved by Fritzing 1.0.2b)
circuit board: 4cm x 6cm
perfboards: 1

parts:
  D1 = LTE-302 [package=lte-302]
  power = Generic female header - 2 pins [form="♀ (female)" package=THT]
  Q1 = NPN-Transistor [package="TO92 [THT]"]
  U1 = ESP32S-HiLetgo [part_number=ESP32]
  sensor = Generic female header - 3 pins [form="♀ (female)" package=THT]
  R1 = Resistor [tolerance=±5% resistance=11 package="0805 [SMD]"]
  R2 = Resistor [tolerance=±5% resistance=1k package="0805 [SMD]"]

nets:
  N1: D1.A, R1.Pin_1
  N2: D1.C, Q1.C
  GND: power.GND, Q1.E, U1.GND, sensor.GND
  VCC: power.VCC, U1.VIN
  N3: Q1.B, R2.Pin_0
  N4: U1.3.3, sensor.VCC, R1.Pin_0
  N5: U1.GPIO27, R2.Pin_1
  N6: U1.GPIO14, sensor.OUT

custom parts:
  Generic female header - 2 pins: Generic female header
  ESP32S-HiLetgo: HiLetgo ESP-WROOM-32 ESP32 ESP-32S Development Board 2.4GHz Dual-Mode WiFi + Bluetooth Dual Cores Microcontroller The ESP32 integrated with Antenna switches, RF Balun, power amplifiers, low-noise amplifiers, filters, and management modules, and the entire solution occupies the least area of PCB. 2.4 GHz Wi-Fi plus Bluetooth dual-mode chip, with TSMC Ultra-low power consumption 40nm technology,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
  Generic female header - 3 pins: Generic female header
